# Fritzing sketch Final_Project_Diagram (saved by Fritzing 0.9.2b)
breadboards: 1

parts:
  Part1 = Arduino Uno (Rev3)
  R1 = Resistor [tolerance=±5% resistance=220 package=THT]
  R2 = Trimmer Potentiometer [maximum_resistance=10kΩ package=THT]
  S1 = Pushbutton [package="[THT]"]
  R3 = Photocell (LDR) [package=THT]
  LED1 = LED - 5mm [color="Red (633nm)" package="5 mm [THT]"]
  M1 = DC Motor
  IC1 = H-Bridge [package=THT]
  J1 = Piezo Speaker
  R4 = Trimmer Potentiometer [maximum_resistance=10kΩ package=THT]
  R5 = Resistor [tolerance=±5% resistance=220 package=THT]
  LED2 = smd LED [color="Red (633nm)" package="0603 [SMD]"]
  LED3 = LED - 5mm [color="Green (560nm)" package="5 mm [THT]"]
  R6 = Resistor [tolerance=±5% resistance=10k package=THT]
  S2 = Pushbutton [package="[THT]"]
  S3 = Pushbutton [package="[THT]"]
  R8 = Resistor [tolerance=±5% resistance=10k package=THT]
  R10 = Resistor [tolerance=±5% resistance=10k package=THT]
  R11 = Resistor [tolerance=±5% resistance=10k package=THT]
  LED4 = LED - 5mm [color="Green (560nm)" package="5 mm [THT]"]
  LED5 = LED - 5mm [color="Yellow (592nm)" package="5 mm [THT]"]
  LED6 = LED - 5mm [color="Yellow (592nm)" package="5 mm [THT]"]
  R12 = Resistor [tolerance=±5% resistance=220 package=THT]
  R13 = Resistor [tolerance=±5% resistance=220 package=THT]
  R14 = Resistor [tolerance=±5% resistance=220 package=THT]

nets:
  N1: Part1.A0, R3.pin_0, R6.Pin_1
  N2: Part1.A1, R2.wiper
  N3: Part1.A2, R4.wiper
  N4: Part1.A3, S3.Pin_3, S3.Pin_4, R11.Pin_1
  N5: Part1.D8, R13.Pin_1
  N6: Part1.D9_PWM, IC1.1_2EN
  N7: Part1.D10_PWM/SS, IC1.1A
  N8: Part1.D11_PWM/MOSI, IC1.2A
  N9: Part1.D12/MISO, R14.Pin_1
  N10: Part1.D13/SCK, LED4.anode
  N11: Part1.D2, J1.pin1
  N12: Part1.D3_PWM, S2.Pin_3, S2.Pin_4, R8.Pin_1
  N13: Part1.D4, S1.Pin_3, S1.Pin_4, R10.Pin_1
  N14: Part1.D5_PWM, R5.Pin_0
  N15: Part1.D6_PWM, R1.Pin_1
  N16: Part1.D7, R12.Pin_1
  N17: Part1.5V, R2.leg1, S1.Pin_1, S1.Pin_2, IC1.VCC2, IC1.VCC1, R4.leg1, R6.Pin_0, S2.Pin_1, S2.Pin_2, S3.Pin_1, S3.Pin_2
  GND: Part1.GND, R2.leg2, R3.pin_1, IC1.GND1, IC1.GND2, IC1.GND3, IC1.GND4, J1.pin2, R4.leg2, LED2.cathode, LED3.cathode, R8.Pin_0, R10.Pin_0, R11.Pin_0
  N18: R1.Pin_0, LED3.anode
  N19: LED1.anode, R14.Pin_0
  N20: M1.pin_1, IC1.1Y
  N21: M1.pin_2, IC1.2Y
  N22: R5.Pin_1, LED2.anode
  N23: LED5.anode, R13.Pin_0
  N24: LED6.anode, R12.Pin_0
